// Logisim project cu.circ as structural Verilog: 1 circuit, main circuit main
module main (
  input  [7:0] in_1,
  input  RUN,
  input  RESET,
  input  CLOCK,
  output out_5,
  output out_6,
  output out_7,
  output out_8,
  output out_9,
  output out_10,
  output out_11,
  output out_12,
  output out_13,
  output out_14,
  output out_15,
  output out_16,
  output out_17,
  output out_18,
  output out_19,
  output out_20,
  output out_21,
  output out_22,
  output out_23,
  output out_24,
  output out_25,
  output out_26
);

  wire and_1_out, and_2_out, not_1_out, not_2_out, not_3_out, or_1_out, t_ff_1_qn;
  wire [1:0] t_ff_1_q;
  wire [10:3] decoder_1_out7;
  wire [21:0] bit_extender_1_out, multiplexer_1_out, multiplexer_3_out, multiplexer_4_out, multiplexer_5_out,
       or_2_out;
  wire [21:14] decoder_2_out7;

  not not_1 (not_1_out, t_ff_1_q[1]);
  not not_2 (not_2_out, t_ff_1_q[0]);
  and and_1 (and_1_out, t_ff_1_q[1], not_2_out, ~in_1[7]);  // AND_Gate
  and and_2 (and_2_out, RUN, not_1_out, not_2_out);
  assign bit_extender_1_out = {{21{1'b0}}, and_2_out};  // Bit_Extender bit_extender_1
  or or_1 (or_1_out, ~RUN, and_1_out, RESET);  // OR_Gate
  T_Flip_Flop t_ff_1 (.clk(CLOCK), .T(1'b1), .Q(t_ff_1_q[0]), .Qn(t_ff_1_qn), .reset(or_1_out));  // open: preset, en
  T_Flip_Flop t_ff_2 (.clk(t_ff_1_qn), .T(1'b1), .Q(t_ff_1_q[1]), .reset(or_1_out));  // open: Qn, preset, en
  Multiplexer #(.select(2), .width(22), .enable("false")) multiplexer_1 (
    .in0(bit_extender_1_out), .in1(multiplexer_5_out), .in2(multiplexer_3_out), .in3(multiplexer_4_out),
    .out(multiplexer_1_out), .sel(t_ff_1_q));
  Multiplexer #(.width(22), .enable("false")) multiplexer_2 (
    .in0({22{1'b0}}), .in1(multiplexer_1_out),
    .out({out_26, out_25, out_24, out_23, out_22, out_21, out_20, out_19, out_18, out_17, out_16, out_15, out_14, out_13, out_12, out_11, out_10, out_9, out_8, out_7, out_6, out_5}),
    .sel(not_3_out));
  not not_3 (not_3_out, RESET);
  Multiplexer #(.select(2), .width(22), .enable("false")) multiplexer_3 (
    .in0({22{1'b0}}), .in1({22{1'b0}}), .in2({11'h2, decoder_1_out7, 3'b000}), .in3(or_2_out),
    .out(multiplexer_3_out), .sel(in_1[7:6]));
  Multiplexer #(.select(2), .width(22), .enable("false")) multiplexer_4 (
    .in0({22{1'b0}}), .in1({22{1'b0}}), .in2({decoder_2_out7, 14'h4}), .in3({decoder_2_out7, 14'h4}),
    .out(multiplexer_4_out), .sel(in_1[7:6]));
  Multiplexer #(.select(2), .width(22), .enable("false")) multiplexer_5 (
    .in0({decoder_2_out7, 3'b000, decoder_1_out7, 3'b000}), .in1({decoder_2_out7, 14'h2}),
    .in2({11'h4, decoder_2_out7, 3'b000}), .in3({11'h4, decoder_2_out7, 3'b000}), .out(multiplexer_5_out),
    .sel(in_1[7:6]));
  assign or_2_out = {11'h2, decoder_1_out7, 3'b000} | 22'h800;  // OR_Gate or_2, 22 bits wide
  Decoder #(.select(3), .enable("false")) decoder_1 (
    .out0(decoder_1_out7[10]), .out1(decoder_1_out7[9]), .out2(decoder_1_out7[8]), .out3(decoder_1_out7[7]),
    .out4(decoder_1_out7[6]), .out5(decoder_1_out7[5]), .out6(decoder_1_out7[4]), .out7(decoder_1_out7[3]),
    .sel(in_1[2:0]));
  Decoder #(.select(3), .enable("false")) decoder_2 (
    .out0(decoder_2_out7[21]), .out1(decoder_2_out7[20]), .out2(decoder_2_out7[19]),
    .out3(decoder_2_out7[18]), .out4(decoder_2_out7[17]), .out5(decoder_2_out7[16]),
    .out6(decoder_2_out7[15]), .out7(decoder_2_out7[14]), .sel(in_1[5:3]));
endmodule
