// Logisim project main.circ as structural Verilog: 1 circuit, main circuit main
module main (
  input  [7:0] Din,
  input  Run,
  input  Reset,
  output [7:0] Bus
);

  wire clock_1_out, main_1_out_5, main_1_out_6, main_1_out_7, main_1_out_8, main_1_out_9, main_1_out_10,
       main_1_out_11, main_1_out_12, main_1_out_13, main_1_out_14, main_1_out_15, main_1_out_16,
       main_1_out_17, main_1_out_18, main_1_out_19, main_1_out_20, main_1_out_21, main_1_out_22,
       main_1_out_23, main_1_out_24, main_1_out_25, main_1_out_26;
  wire [7:0] A_q, adder_1_out, B_q, IR_q, multiplexer_1_out, multiplexer_2_out, multiplexer_3_out,
       multiplexer_4_out, multiplexer_5_out, multiplexer_6_out, multiplexer_7_out, multiplexer_8_out,
       multiplexer_9_out, multiplexer_10_out, multiplexer_11_out, R0_q, R1_q, R2_q, R3_q, R4_q, R5_q, R6_q,
       R7_q, subtractor_1_out;

  Clock clock_1 (.out(clock_1_out));
  Multiplexer #(.width(8), .enable("false")) multiplexer_1 (
    .in0({8{1'b0}}), .in1(Din), .out(multiplexer_1_out), .sel(main_1_out_6));
  Register IR (.D(Din), .en(main_1_out_5), .Q(IR_q), .clk(clock_1_out));  // open: clr
  Multiplexer #(.width(8), .enable("false")) multiplexer_2 (
    .in0({8{1'b0}}), .in1(R0_q), .out(multiplexer_2_out), .sel(main_1_out_15));
  Register R0 (.D(Bus), .en(main_1_out_26), .Q(R0_q), .clk(clock_1_out));  // open: clr
  Multiplexer #(.width(8), .enable("false")) multiplexer_3 (
    .in0({8{1'b0}}), .in1(R1_q), .out(multiplexer_3_out), .sel(main_1_out_14));
  Register R2 (.D(Bus), .en(main_1_out_24), .Q(R2_q), .clk(clock_1_out));  // open: clr
  Register R1 (.D(Bus), .en(main_1_out_25), .Q(R1_q), .clk(clock_1_out));  // open: clr
  Multiplexer #(.width(8), .enable("false")) multiplexer_4 (
    .in0({8{1'b0}}), .in1(R2_q), .out(multiplexer_4_out), .sel(main_1_out_13));
  Register R3 (.D(Bus), .en(main_1_out_23), .Q(R3_q), .clk(clock_1_out));  // open: clr
  Multiplexer #(.width(8), .enable("false")) multiplexer_5 (
    .in0({8{1'b0}}), .in1(R3_q), .out(multiplexer_5_out), .sel(main_1_out_12));
  assign Bus = multiplexer_1_out | multiplexer_2_out | multiplexer_3_out | multiplexer_4_out | multiplexer_5_out | multiplexer_6_out | multiplexer_7_out | multiplexer_8_out | multiplexer_9_out | multiplexer_10_out;  // OR_Gate or_1, 8 bits wide
  cu_main main_1 (
    .in_1(IR_q), .RUN(Run), .RESET(Reset), .CLOCK(clock_1_out), .out_5(main_1_out_5), .out_6(main_1_out_6),
    .out_7(main_1_out_7), .out_8(main_1_out_8), .out_9(main_1_out_9), .out_10(main_1_out_10),
    .out_11(main_1_out_11), .out_12(main_1_out_12), .out_13(main_1_out_13), .out_14(main_1_out_14),
    .out_15(main_1_out_15), .out_16(main_1_out_16), .out_17(main_1_out_17), .out_18(main_1_out_18),
    .out_19(main_1_out_19), .out_20(main_1_out_20), .out_21(main_1_out_21), .out_22(main_1_out_22),
    .out_23(main_1_out_23), .out_24(main_1_out_24), .out_25(main_1_out_25), .out_26(main_1_out_26));
  Register R4 (.D(Bus), .en(main_1_out_22), .Q(R4_q), .clk(clock_1_out));  // open: clr
  Multiplexer #(.width(8), .enable("false")) multiplexer_6 (
    .in0({8{1'b0}}), .in1(R4_q), .out(multiplexer_6_out), .sel(main_1_out_11));
  Register R6 (.D(Bus), .en(main_1_out_20), .Q(R6_q), .clk(clock_1_out));  // open: clr
  Register R5 (.D(Bus), .en(main_1_out_21), .Q(R5_q), .clk(clock_1_out));  // open: clr
  Multiplexer #(.width(8), .enable("false")) multiplexer_7 (
    .in0({8{1'b0}}), .in1(R5_q), .out(multiplexer_7_out), .sel(main_1_out_10));
  Multiplexer #(.width(8), .enable("false")) multiplexer_8 (
    .in0({8{1'b0}}), .in1(R6_q), .out(multiplexer_8_out), .sel(main_1_out_9));
  Register R7 (.D(Bus), .en(main_1_out_19), .Q(R7_q), .clk(clock_1_out));  // open: clr
  Multiplexer #(.width(8), .enable("false")) multiplexer_9 (
    .in0({8{1'b0}}), .in1(R7_q), .out(multiplexer_9_out), .sel(main_1_out_8));
  Multiplexer #(.width(8), .enable("false")) multiplexer_10 (
    .in0({8{1'b0}}), .in1(B_q), .out(multiplexer_10_out), .sel(main_1_out_7));
  Register A (.D(Bus), .en(main_1_out_18), .Q(A_q), .clk(clock_1_out));  // open: clr
  Adder adder_1 (.a(A_q), .b(Bus), .out(adder_1_out));  // open: cin, cout
  Multiplexer #(.width(8), .enable("false")) multiplexer_11 (
    .in0(adder_1_out), .in1(subtractor_1_out), .out(multiplexer_11_out), .sel(main_1_out_16));
  Subtractor subtractor_1 (.a(A_q), .b(Bus), .out(subtractor_1_out));  // open: bin, bout
  Register B (.D(multiplexer_11_out), .en(main_1_out_17), .Q(B_q), .clk(clock_1_out));  // open: clr
endmodule
